// Logisim project 171044041.circ as structural Verilog: 14 circuits, main circuit main
module main (
  input  START,
  input  RESET,
  input  [31:0] in_3,
  input  [31:0] in_4,
  output [7:0] out_5
);

  wire A_out, B_out, C_out, clock_1_out, control_unit_1_lsp, control_unit_1_prntall, control_unit_1_res,
       control_unit_1_sc, control_unit_1_ss, control_unit_1_stty, control_unit_1_winp, D_out,
       data_path_1_lose, data_path_1_print, data_path_1_print_finish, data_path_1_reset_screen,
       data_path_1_win, E_out, F_out, G_out, H_out, I_out, inputsync_1_o, J_out, K_out, L_out, not_1_out,
       or_1_out, priority_encoder_1_p1, priority_encoder_1_p14, priority_encoder_1_p15,
       priority_encoder_1_p16, priority_encoder_1_p18, priority_encoder_1_p19, priority_encoder_1_p20,
       priority_encoder_1_p21, priority_encoder_1_p22, priority_encoder_1_p23, priority_encoder_1_p24,
       priority_encoder_1_p25, priority_encoder_1_p26, priority_encoder_1_p27, priority_encoder_1_p28;
  wire [4:0] priority_encoder_1_p17;
  wire [5:0] data_path_1_number_of_wrong_guess, data_path_1_number_of_wrong_guess_2,
       data_path_1_number_of_wrong_guess_3, data_path_1_number_of_wrong_guess_4,
       data_path_1_number_of_wrong_guess_5;
  wire [6:0] data_path_1_letter, data_path_1_number_of_letters_7bit_segment_form,
       data_path_1_number_of_lose_7bit_segment_form, data_path_1_number_of_wins_7bit_segment_form;

  Button A (.out(A_out));
  Button C (.out(C_out));
  Button B (.out(B_out));
  Button D (.out(D_out));
  Clock clock_1 (.out(clock_1_out));
  Button E (.out(E_out));
  Button F (.out(F_out));
  Button G (.out(G_out));
  not not_1 (not_1_out, priority_encoder_1_p1);
  Button I (.out(I_out));
  Button H (.out(H_out));
  InputSync inputsync_1 (.I(not_1_out), .CLK(clock_1_out), .O(inputsync_1_o));
  Button J (.out(J_out));
  Button K (.out(K_out));
  Register register_1 (
    .D({3'b011, priority_encoder_1_p17}), .en(inputsync_1_o), .Q(out_5), .clk(clock_1_out));  // open: clr
  Control_Unit control_unit_1 (
    .GO(START), .PrintFinish(data_path_1_print_finish), .Lose(data_path_1_lose), .Win(data_path_1_win),
    .Button(inputsync_1_o), .CLK(clock_1_out), .Reset(RESET), .SC(control_unit_1_sc), .SS(control_unit_1_ss),
    .RES(control_unit_1_res), .STTY(control_unit_1_stty), .PRNTALL(control_unit_1_prntall),
    .WINP(control_unit_1_winp), .LSP(control_unit_1_lsp));  // open: out_15
  Button L (.out(L_out));
  // Priority_Encoder #(.select(5)) priority_encoder_1: pin names not known; wires that end beside it: priority_encoder_1_p1, A_out, B_out, C_out, D_out, E_out, F_out, G_out, H_out, I_out, J_out, K_out, L_out, priority_encoder_1_p14, priority_encoder_1_p15, priority_encoder_1_p16, priority_encoder_1_p17, priority_encoder_1_p18, priority_encoder_1_p19, priority_encoder_1_p20, priority_encoder_1_p21, priority_encoder_1_p22, priority_encoder_1_p23, priority_encoder_1_p24, priority_encoder_1_p25, priority_encoder_1_p26, priority_encoder_1_p27, priority_encoder_1_p28
  DotMatrix #(.matrixrows(6)) dotmatrix_1 (
    .col0(data_path_1_number_of_wrong_guess_5), .col1(data_path_1_number_of_wrong_guess_4),
    .col2(data_path_1_number_of_wrong_guess_3), .col3(data_path_1_number_of_wrong_guess_2),
    .col4(data_path_1_number_of_wrong_guess));
  Button N (.out(priority_encoder_1_p15));
  Button M (.out(priority_encoder_1_p14));
  Button O (.out(priority_encoder_1_p16));
  Button P (.out(priority_encoder_1_p18));
  Button Q (.out(priority_encoder_1_p19));
  Data_Path data_path_1 (
    .First_4_Latter(in_3), .Last_4_Latter(in_4), .Guess(out_5), .Select_Compare(control_unit_1_sc),
    .Start_Set(control_unit_1_ss), .Reset(control_unit_1_res), .Start_TTY(control_unit_1_stty),
    .Print_All(control_unit_1_prntall), .WinPoint(control_unit_1_winp), .LosePoint(control_unit_1_lsp),
    .CLK(clock_1_out),
    .Number_of_wrong_guess({data_path_1_number_of_wrong_guess_5, data_path_1_number_of_wrong_guess_4, data_path_1_number_of_wrong_guess_3, data_path_1_number_of_wrong_guess_2, data_path_1_number_of_wrong_guess}),
    .Number_Of_Letters_7bit_segment_form(data_path_1_number_of_letters_7bit_segment_form),
    .Lose(data_path_1_lose), .Number_Of_Wins_7bit_segment_form(data_path_1_number_of_wins_7bit_segment_form),
    .Print_Finish(data_path_1_print_finish), .Letter(data_path_1_letter), .Print(data_path_1_print),
    .Reset_Screen(data_path_1_reset_screen), .Win(data_path_1_win),
    .Number_Of_Lose_7bit_segment_form(data_path_1_number_of_lose_7bit_segment_form));
  TTY tty_1 (.data(data_path_1_letter), .clk(clock_1_out), .we(data_path_1_print), .clr(or_1_out));
  Button S (.out(priority_encoder_1_p21));
  Button R (.out(priority_encoder_1_p20));
  or or_1 (or_1_out, data_path_1_reset_screen, RESET);
  Button T (.out(priority_encoder_1_p22));
  Button V (.out(priority_encoder_1_p24));
  Button U (.out(priority_encoder_1_p23));
  Button W (.out(priority_encoder_1_p25));
  Button X (.out(priority_encoder_1_p26));
  Button Y (.out(priority_encoder_1_p27));
  Button Z (.out(priority_encoder_1_p28));
  _7_Segment_Display u_7_segment_display_1 (
    .g(data_path_1_number_of_letters_7bit_segment_form[6]),
    .f(data_path_1_number_of_letters_7bit_segment_form[5]),
    .a(data_path_1_number_of_letters_7bit_segment_form[0]),
    .b(data_path_1_number_of_letters_7bit_segment_form[1]),
    .e(data_path_1_number_of_letters_7bit_segment_form[4]),
    .d(data_path_1_number_of_letters_7bit_segment_form[3]),
    .c(data_path_1_number_of_letters_7bit_segment_form[2]));  // open: dp
  _7_Segment_Display u_7_segment_display_2 (
    .g(data_path_1_number_of_wins_7bit_segment_form[6]), .f(data_path_1_number_of_wins_7bit_segment_form[5]),
    .a(data_path_1_number_of_wins_7bit_segment_form[0]), .b(data_path_1_number_of_wins_7bit_segment_form[1]),
    .e(data_path_1_number_of_wins_7bit_segment_form[4]), .d(data_path_1_number_of_wins_7bit_segment_form[3]),
    .c(data_path_1_number_of_wins_7bit_segment_form[2]));  // open: dp
  _7_Segment_Display u_7_segment_display_3 (
    .g(data_path_1_number_of_lose_7bit_segment_form[6]), .f(data_path_1_number_of_lose_7bit_segment_form[5]),
    .a(data_path_1_number_of_lose_7bit_segment_form[0]), .b(data_path_1_number_of_lose_7bit_segment_form[1]),
    .e(data_path_1_number_of_lose_7bit_segment_form[4]), .d(data_path_1_number_of_lose_7bit_segment_form[3]),
    .c(data_path_1_number_of_lose_7bit_segment_form[2]));  // open: dp

  // Notes on the sheet:
  //   First 4 Letter
  //   Last 4 Letter
  //   Hangman
  //   Letters
  //   User Point
  //   Number of letters
  //   Computer Point
endmodule

module Control_Unit (
  input  GO,
  input  PrintFinish,
  input  Lose,
  input  Win,
  input  Button,
  input  CLK,
  input  Reset,
  output SC,
  output SS,
  output RES,
  output STTY,
  output PRNTALL,
  output WINP,
  output LSP,
  output [2:0] out_15
);

  wire and_1_out, and_2_out, and_3_out, and_4_out, and_5_out, and_6_out, and_7_out, and_8_out, and_9_out,
       and_10_out, and_11_out, and_12_out, and_13_out, and_17_out, and_18_out, not_1_out, not_2_out,
       not_3_out, not_4_out, not_5_out, not_6_out, not_7_out, not_8_out, not_9_out, not_10_out, not_11_out,
       not_12_out, not_13_out, not_14_out, not_15_out, not_16_out, not_17_out, not_18_out, not_19_out,
       not_20_out, not_21_out, not_22_out, not_23_out, not_24_out, not_25_out, not_26_out, not_27_out,
       not_28_out, not_29_out, not_30_out, not_31_out, not_32_out, not_33_out, not_34_out, not_35_out,
       not_36_out, not_37_out, not_38_out, or_1_out;
  wire [2:0] or_4_out;

  or or_1 (or_1_out, Lose, Win);
  Register #(.width(3)) register_1 (.D(or_4_out), .en(1'b1), .Q(out_15), .clk(CLK), .clr(Reset));
  not not_1 (not_1_out, out_15[0]);
  not not_2 (not_2_out, Lose);
  not not_3 (not_3_out, Button);
  not not_4 (not_4_out, out_15[2]);
  not not_5 (not_5_out, out_15[0]);
  not not_6 (not_6_out, Lose);
  not not_7 (not_7_out, out_15[2]);
  not not_8 (not_8_out, out_15[0]);
  not not_9 (not_9_out, Win);
  not not_10 (not_10_out, out_15[1]);
  not not_11 (not_11_out, out_15[0]);
  not not_12 (not_12_out, Button);
  not not_13 (not_13_out, out_15[2]);
  not not_14 (not_14_out, out_15[0]);
  not not_15 (not_15_out, PrintFinish);
  not not_16 (not_16_out, out_15[0]);
  not not_17 (not_17_out, Lose);
  not not_18 (not_18_out, Win);
  not not_19 (not_19_out, out_15[0]);
  not not_20 (not_20_out, out_15[2]);
  not not_21 (not_21_out, out_15[1]);
  not not_22 (not_22_out, out_15[0]);
  not not_23 (not_23_out, out_15[2]);
  not not_24 (not_24_out, out_15[0]);
  not not_25 (not_25_out, Win);
  not not_26 (not_26_out, out_15[1]);
  not not_27 (not_27_out, out_15[0]);
  and and_1 (and_1_out, out_15[1], not_1_out, PrintFinish, not_2_out, not_3_out);
  and and_2 (and_2_out, not_4_out, out_15[1], not_5_out, PrintFinish, not_6_out, Win);
  and and_3 (and_3_out, not_7_out, out_15[1], not_8_out, PrintFinish, Lose, not_9_out);
  and and_4 (and_4_out, out_15[2], not_10_out);
  and and_5 (and_5_out, out_15[2], not_11_out, not_12_out);
  and and_6 (and_6_out, not_13_out, out_15[0]);
  and and_7 (and_7_out, out_15[1], not_14_out, not_15_out);
  and and_8 (and_8_out, out_15[1], not_16_out, not_17_out, not_18_out);
  and and_9 (and_9_out, out_15[2], out_15[1], not_19_out);
  and and_10 (and_10_out, not_20_out, not_21_out, not_22_out, GO);
  and and_11 (and_11_out, not_23_out, out_15[1], not_24_out, PrintFinish, Lose, not_25_out);
  and and_12 (and_12_out, out_15[2], not_26_out, out_15[0]);
  and and_13 (and_13_out, out_15[2], out_15[1], not_27_out, Button);
  or or_2 (or_4_out[2], and_1_out, and_2_out, and_3_out, and_4_out, and_5_out);
  or or_3 (or_4_out[1], and_6_out, and_7_out, and_8_out, and_9_out);
  or or_4 (or_4_out[0], and_10_out, and_11_out, and_12_out, and_13_out);
  and and_14 (SC, out_15[1], out_15[0]);
  not not_28 (not_28_out, out_15[2]);
  not not_29 (not_29_out, out_15[1]);
  not not_30 (not_30_out, out_15[2]);
  not not_31 (not_31_out, out_15[1]);
  not not_32 (not_32_out, out_15[0]);
  not not_33 (not_33_out, out_15[2]);
  not not_34 (not_34_out, out_15[0]);
  not not_35 (not_35_out, out_15[2]);
  not not_36 (not_36_out, out_15[0]);
  not not_37 (not_37_out, out_15[1]);
  not not_38 (not_38_out, out_15[0]);
  and and_15 (LSP, out_15[2], out_15[0]);
  and and_16 (SS, not_28_out, not_29_out, out_15[0]);
  and and_17 (and_17_out, not_30_out, not_31_out, not_32_out);
  or or_5 (RES, and_17_out, and_18_out);
  and and_18 (and_18_out, out_15[2], out_15[1], out_15[0]);
  and and_19 (STTY, not_33_out, out_15[1], not_34_out);
  and and_20 (PRNTALL, not_35_out, out_15[1], not_36_out, or_1_out);
  and and_21 (WINP, out_15[2], not_37_out, not_38_out);
endmodule

module Data_Path (
  input  [31:0] First_4_Latter,
  input  [31:0] Last_4_Latter,
  input  [7:0] Guess,
  input  Select_Compare,
  input  Start_Set,
  input  Reset,
  input  Start_TTY,
  input  Print_All,
  input  WinPoint,
  input  LosePoint,
  input  CLK,
  output [29:0] Number_of_wrong_guess,
  output [6:0] Number_Of_Letters_7bit_segment_form,
  output Lose,
  output [6:0] Number_Of_Wins_7bit_segment_form,
  output Print_Finish,
  output [6:0] Letter,
  output Print,
  output Reset_Screen,
  output Win,
  output [6:0] Number_Of_Lose_7bit_segment_form
);

  wire _8_Bit_OR_result, and_1_out, inputsync_1_o, inputsync_2_o, not_1_out;
  wire [3:0] counter_1_q, Letter_Count_number_of_letters, Lose_Count_q, Win_Count_q;
  wire [7:0] bit_extender_1_out, letter_register_5_letter_2, letter_register_7_letter_2,
       letter_register_8_isfound, letter_register_8_letter_2, letter_register_8_recentlyfound;
  wire [23:16] letter_register_6_letter_2;
  wire [31:0] letter_register_4_letter_2;

  TTYController ttycontroller_1 (
    .StartTTY(Start_TTY), .Print_All(Print_All), .First_4_Latter(letter_register_4_letter_2),
    .Last_4_Latter({letter_register_5_letter_2, letter_register_6_letter_2, letter_register_7_letter_2, letter_register_8_letter_2}),
    .isFounds(letter_register_8_isfound), .CLK(CLK), .PrintFinish(Print_Finish), .Letter_to_print(Letter),
    .Print(Print), .Reset_Screen(Reset_Screen));
  LetterCount Letter_Count (
    .First_4_Latter(First_4_Latter), .Last_4_Latter(Last_4_Latter), .Load_Letter_Count(Start_Set),
    .Re(Reset), .CLK(CLK), .Number_of_letters(Letter_Count_number_of_letters));
  _7SegmentConverter Converter (
    ._4Bit_Input(Letter_Count_number_of_letters), ._7Bit_Segment(Number_Of_Letters_7bit_segment_form));
  Letter_Register letter_register_1 (
    .Letter(First_4_Latter[31:24]), .Guess(Guess), .SelectCompare(Select_Compare), .LoadLetter(Start_Set),
    .Reset(Reset), .CLK(CLK), .RecentlyFound(letter_register_8_recentlyfound[7]),
    .isFound(letter_register_8_isfound[7]), .Letter_2(letter_register_4_letter_2[31:24]));
  _8BitAND _8_Bit_AND (.Bits(letter_register_8_isfound), .Result(Win));
  Letter_Register letter_register_2 (
    .Letter(First_4_Latter[23:16]), .Guess(Guess), .SelectCompare(Select_Compare), .LoadLetter(Start_Set),
    .Reset(Reset), .CLK(CLK), .RecentlyFound(letter_register_8_recentlyfound[6]),
    .isFound(letter_register_8_isfound[6]), .Letter_2(letter_register_4_letter_2[23:16]));
  InputSync inputsync_1 (.I(LosePoint), .CLK(CLK), .O(inputsync_1_o));
  Letter_Register letter_register_3 (
    .Letter(First_4_Latter[15:8]), .Guess(Guess), .SelectCompare(Select_Compare), .LoadLetter(Start_Set),
    .Reset(Reset), .CLK(CLK), .RecentlyFound(letter_register_8_recentlyfound[5]),
    .isFound(letter_register_8_isfound[5]), .Letter_2(letter_register_4_letter_2[15:8]));
  InputSync inputsync_2 (.I(WinPoint), .CLK(CLK), .O(inputsync_2_o));
  Letter_Register letter_register_4 (
    .Letter(First_4_Latter[7:0]), .Guess(Guess), .SelectCompare(Select_Compare), .LoadLetter(Start_Set),
    .Reset(Reset), .CLK(CLK), .RecentlyFound(letter_register_8_recentlyfound[4]),
    .isFound(letter_register_8_isfound[4]), .Letter_2(letter_register_4_letter_2[7:0]));
  _7SegmentConverter Converter_2 (._4Bit_Input(Win_Count_q), ._7Bit_Segment(Number_Of_Wins_7bit_segment_form));
  Counter #(.width(4), .max('hf)) Win_Count (
    .count(inputsync_2_o), .Q(Win_Count_q), .clk(CLK));  // open: load, D, carry, clr
  Counter #(.width(4), .max('hf)) Lose_Count (
    .count(inputsync_1_o), .Q(Lose_Count_q), .clk(CLK));  // open: load, D, carry, clr
  _7SegmentConverter Converter_3 (._4Bit_Input(Lose_Count_q), ._7Bit_Segment(Number_Of_Lose_7bit_segment_form));
  Letter_Register letter_register_5 (
    .Letter(Last_4_Latter[31:24]), .Guess(Guess), .SelectCompare(Select_Compare), .LoadLetter(Start_Set),
    .Reset(Reset), .CLK(CLK), .RecentlyFound(letter_register_8_recentlyfound[3]),
    .isFound(letter_register_8_isfound[3]), .Letter_2(letter_register_5_letter_2));
  _8BitOR _8_Bit_OR (.Bits(letter_register_8_recentlyfound), .Result(_8_Bit_OR_result));
  Letter_Register letter_register_6 (
    .Letter(Last_4_Latter[23:16]), .Guess(Guess), .SelectCompare(Select_Compare), .LoadLetter(Start_Set),
    .Reset(Reset), .CLK(CLK), .RecentlyFound(letter_register_8_recentlyfound[2]),
    .isFound(letter_register_8_isfound[2]), .Letter_2(letter_register_6_letter_2));
  not not_1 (not_1_out, _8_Bit_OR_result);
  and and_1 (and_1_out, Select_Compare, not_1_out);
  Letter_Register letter_register_7 (
    .Letter(Last_4_Latter[15:8]), .Guess(Guess), .SelectCompare(Select_Compare), .LoadLetter(Start_Set),
    .Reset(Reset), .CLK(CLK), .RecentlyFound(letter_register_8_recentlyfound[1]),
    .isFound(letter_register_8_isfound[1]), .Letter_2(letter_register_7_letter_2));
  Counter #(.width(4), .max('hf)) counter_1 (
    .count(and_1_out), .Q(counter_1_q), .clk(CLK), .clr(Reset));  // open: load, D, carry
  Letter_Register letter_register_8 (
    .Letter(Last_4_Latter[7:0]), .Guess(Guess), .SelectCompare(Select_Compare), .LoadLetter(Start_Set),
    .Reset(Reset), .CLK(CLK), .RecentlyFound(letter_register_8_recentlyfound[0]),
    .isFound(letter_register_8_isfound[0]), .Letter_2(letter_register_8_letter_2));
  assign bit_extender_1_out = {{4{1'b0}}, counter_1_q};  // Bit_Extender bit_extender_1
  Draw_Hangman draw_hangman_1 (.Number_of_wrong_guess(counter_1_q), .out_2(Number_of_wrong_guess));
  _8BitEqualityChecker u_8bitequalitychecker_1 (.First(bit_extender_1_out), .Second(8'ha), .Equal(Lose));

  // Notes on the sheet:
  //   wrong guess count
  //   isFounds
  //   RecentlyFounds
endmodule

module LetterCount (
  input  [31:0] First_4_Latter,
  input  [31:0] Last_4_Latter,
  input  Load_Letter_Count,
  input  Re,
  input  CLK,
  output [3:0] Number_of_letters
);

  wire and_1_out, and_2_out, and_3_out, and_4_out, and_5_out, and_6_out, and_7_out, iszero_1_out_2,
       iszero_2_out_2, iszero_3_out_2, iszero_4_out_2, iszero_5_out_2, iszero_6_out_2, iszero_7_out_2,
       iszero_8_out_2, not_1_out, not_2_out, not_3_out, not_4_out, not_5_out, not_6_out, not_7_out;
  wire [3:0] or_3_out;

  isZero iszero_1 (.Bits(First_4_Latter[31:24]), .out_2(iszero_1_out_2));
  isZero iszero_2 (.Bits(First_4_Latter[23:16]), .out_2(iszero_2_out_2));
  isZero iszero_3 (.Bits(First_4_Latter[15:8]), .out_2(iszero_3_out_2));
  isZero iszero_4 (.Bits(First_4_Latter[7:0]), .out_2(iszero_4_out_2));
  isZero iszero_5 (.Bits(Last_4_Latter[31:24]), .out_2(iszero_5_out_2));
  isZero iszero_6 (.Bits(Last_4_Latter[23:16]), .out_2(iszero_6_out_2));
  isZero iszero_7 (.Bits(Last_4_Latter[15:8]), .out_2(iszero_7_out_2));
  isZero iszero_8 (.Bits(Last_4_Latter[7:0]), .out_2(iszero_8_out_2));
  not not_1 (not_1_out, iszero_2_out_2);
  not not_2 (not_2_out, iszero_3_out_2);
  not not_3 (not_3_out, iszero_4_out_2);
  not not_4 (not_4_out, iszero_5_out_2);
  not not_5 (not_5_out, iszero_6_out_2);
  not not_6 (not_6_out, iszero_7_out_2);
  not not_7 (not_7_out, iszero_8_out_2);
  not not_8 (or_3_out[3], iszero_1_out_2);
  and and_1 (and_1_out, iszero_1_out_2, not_1_out);
  and and_2 (and_2_out, iszero_2_out_2, not_2_out);
  and and_3 (and_3_out, iszero_3_out_2, not_3_out);
  and and_4 (and_4_out, iszero_4_out_2, not_4_out);
  and and_5 (and_5_out, iszero_5_out_2, not_5_out);
  and and_6 (and_6_out, iszero_6_out_2, not_6_out);
  and and_7 (and_7_out, iszero_7_out_2, not_7_out);
  Register #(.width(4)) register_1 (.D(or_3_out), .en(Load_Letter_Count), .Q(Number_of_letters), .clk(CLK), .clr(Re));
  or or_1 (or_3_out[2], and_1_out, and_2_out, and_3_out, and_4_out);
  or or_2 (or_3_out[1], and_1_out, and_2_out, and_5_out, and_6_out);
  or or_3 (or_3_out[0], and_1_out, and_3_out, and_5_out, and_7_out);
endmodule

// Letter
module Letter_Register (
  input  [7:0] Letter,
  input  [7:0] Guess,
  input  SelectCompare,
  input  LoadLetter,
  input  Reset,
  input  CLK,
  output RecentlyFound,
  output isFound,
  output [7:0] Letter_2
);

  wire and_1_out, Equality_Checker_equal, not_1_out, or_1_out;
  wire [7:0] multiplexer_1_out, multiplexer_2_out;

  Multiplexer #(.width(8), .enable("false")) multiplexer_1 (
    .in0({8{1'b0}}), .in1(Guess), .out(multiplexer_1_out), .sel(SelectCompare));
  Multiplexer #(.width(8), .enable("false")) multiplexer_2 (
    .in0(Letter), .in1(Letter_2), .out(multiplexer_2_out), .sel(SelectCompare));
  Register u_Letter (.D(Letter), .en(LoadLetter), .Q(Letter_2), .clk(CLK), .clr(Reset));
  and and_1 (and_1_out, LoadLetter, Equality_Checker_equal);
  _8BitEqualityChecker Equality_Checker (
    .First(multiplexer_2_out), .Second(multiplexer_1_out), .Equal(Equality_Checker_equal));
  or or_1 (or_1_out, and_1_out, RecentlyFound);
  not not_1 (not_1_out, isFound);
  Register #(.width(1)) u_isFound (.D(or_1_out), .en(or_1_out), .Q(isFound), .clk(CLK), .clr(Reset));
  and and_2 (RecentlyFound, SelectCompare, Equality_Checker_equal, not_1_out);
endmodule

module _7SegmentConverter (
  input  [3:0] _4Bit_Input,
  output [6:0] _7Bit_Segment
);

  wire and_1_out, and_2_out, and_3_out, and_4_out, and_5_out, and_6_out, and_7_out, and_8_out, and_9_out,
       and_10_out, and_11_out, and_12_out, and_13_out, and_14_out, and_15_out, and_16_out, not_1_out,
       not_2_out, not_3_out, not_4_out, not_5_out, not_6_out, not_7_out, not_8_out, not_9_out, not_10_out,
       not_11_out, not_12_out, not_13_out, not_14_out, not_15_out, not_16_out, not_17_out, not_18_out,
       not_19_out, not_20_out, not_21_out;

  not not_1 (not_1_out, _4Bit_Input[2]);
  not not_2 (not_2_out, _4Bit_Input[0]);
  not not_3 (not_3_out, _4Bit_Input[1]);
  not not_4 (not_4_out, _4Bit_Input[0]);
  not not_5 (not_5_out, _4Bit_Input[1]);
  not not_6 (not_6_out, _4Bit_Input[2]);
  not not_7 (not_7_out, _4Bit_Input[0]);
  not not_8 (not_8_out, _4Bit_Input[2]);
  not not_9 (not_9_out, _4Bit_Input[0]);
  not not_10 (not_10_out, _4Bit_Input[1]);
  not not_11 (not_11_out, _4Bit_Input[2]);
  not not_12 (not_12_out, _4Bit_Input[0]);
  not not_13 (not_13_out, _4Bit_Input[0]);
  not not_14 (not_14_out, _4Bit_Input[1]);
  not not_15 (not_15_out, _4Bit_Input[0]);
  not not_16 (not_16_out, _4Bit_Input[1]);
  not not_17 (not_17_out, _4Bit_Input[0]);
  not not_18 (not_18_out, _4Bit_Input[2]);
  not not_19 (not_19_out, _4Bit_Input[1]);
  not not_20 (not_20_out, _4Bit_Input[0]);
  and and_1 (and_1_out, not_1_out, not_2_out);
  and and_2 (and_2_out, _4Bit_Input[2], _4Bit_Input[0]);
  not not_21 (not_21_out, _4Bit_Input[2]);
  and and_3 (and_3_out, not_3_out, not_4_out);
  and and_4 (and_4_out, _4Bit_Input[1], _4Bit_Input[0]);
  or or_1 (_7Bit_Segment[2], not_5_out, _4Bit_Input[0], _4Bit_Input[2]);
  and and_5 (and_5_out, not_6_out, not_7_out);
  and and_6 (and_6_out, not_8_out, _4Bit_Input[1]);
  and and_7 (and_7_out, _4Bit_Input[1], not_9_out);
  and and_8 (and_8_out, _4Bit_Input[2], not_10_out, _4Bit_Input[0]);
  and and_9 (and_9_out, not_11_out, not_12_out);
  and and_10 (and_10_out, _4Bit_Input[1], not_13_out);
  and and_11 (and_11_out, not_14_out, not_15_out);
  and and_12 (and_12_out, _4Bit_Input[2], not_16_out);
  and and_13 (and_13_out, _4Bit_Input[2], not_17_out);
  and and_14 (and_14_out, not_18_out, _4Bit_Input[1]);
  and and_15 (and_15_out, _4Bit_Input[2], not_19_out);
  and and_16 (and_16_out, _4Bit_Input[2], not_20_out);
  or or_2 (_7Bit_Segment[0], and_1_out, _4Bit_Input[1], and_2_out, _4Bit_Input[3]);
  or or_3 (_7Bit_Segment[1], not_21_out, and_3_out, and_4_out);
  or or_4 (_7Bit_Segment[3], and_5_out, and_6_out, and_7_out, and_8_out, _4Bit_Input[3]);
  or or_5 (_7Bit_Segment[4], and_9_out, and_10_out);
  or or_6 (_7Bit_Segment[5], and_11_out, and_12_out, and_13_out, _4Bit_Input[3]);
  or or_7 (_7Bit_Segment[6], and_14_out, and_15_out, and_16_out, _4Bit_Input[3]);
endmodule

module TTYController (
  input  StartTTY,
  input  Print_All,
  input  [31:0] First_4_Latter,
  input  [31:0] Last_4_Latter,
  input  [7:0] isFounds,
  input  CLK,
  output PrintFinish,
  output [6:0] Letter_to_print,
  output Print,
  output Reset_Screen
);

  wire and_1_out, multiplexer_1_out, n8bitequalitychecker_1_equal, or_1_out, tty_sync_1_printsync;
  wire [2:0] counter_1_q, xnor_1_out;
  wire [7:0] multiplexer_2_out, multiplexer_3_out;

  TTY_Sync tty_sync_1 (.Start(StartTTY), .CLK(CLK), .ResetSync(Reset_Screen), .PrintSync(tty_sync_1_printsync));
  Counter #(.width(3), .max('h7)) counter_1 (
    .count(and_1_out), .Q(counter_1_q), .clk(CLK));  // open: load, D, carry, clr
  and and_1 (and_1_out, tty_sync_1_printsync, StartTTY);
  Multiplexer #(.select(3), .enable("false")) multiplexer_1 (
    .in0(isFounds[7]), .in1(isFounds[6]), .in2(isFounds[5]), .in3(isFounds[4]), .in4(isFounds[3]),
    .in5(isFounds[2]), .in6(isFounds[1]), .in7(isFounds[0]), .out(multiplexer_1_out), .sel(counter_1_q));
  Multiplexer #(.select(3), .width(8), .enable("false")) multiplexer_2 (
    .in0(First_4_Latter[31:24]), .in1(First_4_Latter[23:16]), .in2(First_4_Latter[15:8]),
    .in3(First_4_Latter[7:0]), .in4(Last_4_Latter[31:24]), .in5(Last_4_Latter[23:16]),
    .in6(Last_4_Latter[15:8]), .in7(Last_4_Latter[7:0]), .out(multiplexer_2_out), .sel(counter_1_q));
  assign xnor_1_out = ~(counter_1_q ^ 3'b111);  // XNOR_Gate xnor_1, 3 bits wide
  not not_1 (Print, n8bitequalitychecker_1_equal);
  _8BitEqualityChecker u_8bitequalitychecker_1 (
    .First(multiplexer_2_out), .Second({8{1'b0}}), .Equal(n8bitequalitychecker_1_equal));
  and and_2 (PrintFinish, xnor_1_out[0], xnor_1_out[1], xnor_1_out[2]);
  or or_1 (or_1_out, Print_All, multiplexer_1_out);
  Multiplexer #(.width(8), .enable("false")) multiplexer_3 (
    .in0(8'h23), .in1(multiplexer_2_out), .out(multiplexer_3_out), .sel(or_1_out));
  Bit_Extender #(.out_width(7)) bit_extender_1 (.in(multiplexer_3_out), .out(Letter_to_print));

  // Notes on the sheet:
  //   Comparator
endmodule

module _8BitEqualityChecker (
  input  [7:0] First,
  input  [7:0] Second,
  output Equal
);

  wire xnor_1_out, xnor_2_out, xnor_3_out, xnor_4_out, xnor_5_out, xnor_6_out, xnor_7_out, xnor_8_out;

  xnor xnor_1 (xnor_1_out, First[0], Second[0]);
  xnor xnor_2 (xnor_2_out, First[1], Second[1]);
  xnor xnor_3 (xnor_3_out, First[2], Second[2]);
  xnor xnor_4 (xnor_4_out, First[3], Second[3]);
  xnor xnor_5 (xnor_5_out, First[4], Second[4]);
  xnor xnor_6 (xnor_6_out, First[5], Second[5]);
  xnor xnor_7 (xnor_7_out, First[6], Second[6]);
  xnor xnor_8 (xnor_8_out, First[7], Second[7]);
  and and_1 (Equal, xnor_1_out, xnor_2_out, xnor_3_out, xnor_4_out, xnor_5_out, xnor_6_out, xnor_7_out, xnor_8_out);
endmodule

module _8BitAND (
  input  [7:0] Bits,
  output Result
);

  and and_1 (Result, Bits[0], Bits[1], Bits[2], Bits[3], Bits[4], Bits[5], Bits[6], Bits[7]);
endmodule

module _8BitOR (
  input  [7:0] Bits,
  output Result
);

  or or_1 (Result, Bits[0], Bits[1], Bits[2], Bits[3], Bits[4], Bits[5], Bits[6], Bits[7]);
endmodule

module isZero (
  input  [7:0] Bits,
  output out_2
);

  not not_1 (out_2, Bits[6]);

  // Notes on the sheet:
  //   All letters are in 011xxxxx form. Checking this situtation
endmodule

// TTY ınpSync
module TTY_Sync (
  input  Start,
  input  CLK,
  output ResetSync,
  output PrintSync
);

  wire not_1_out;

  not not_1 (not_1_out, PrintSync);
  and and_1 (ResetSync, not_1_out, Start);
  Register #(.width(1)) register_1 (.D(Start), .en(1'b1), .Q(PrintSync), .clk(CLK));  // open: clr
endmodule

// Input Sync
module InputSync (
  input  I,
  input  CLK,
  output O
);

  wire and_1_out, and_2_out, not_1_out, not_2_out;
  wire [1:0] and_3_out;
  wire [1:1] register_1_q;

  Register #(.width(2)) register_1 (.D(and_3_out), .en(1'b1), .Q({register_1_q[1], O}), .clk(CLK));  // open: clr
  and and_1 (and_1_out, O, I);
  and and_2 (and_2_out, register_1_q[1], I);
  not not_1 (not_1_out, register_1_q[1]);
  not not_2 (not_2_out, O);
  or or_1 (and_3_out[1], and_1_out, and_2_out);
  and and_3 (and_3_out[0], not_1_out, not_2_out, I);
endmodule

module Draw_Hangman (
  input  [3:0] Number_of_wrong_guess,
  output [29:0] out_2
);

  Multiplexer #(.select(4), .width(30), .enable("false")) multiplexer_1 (
    .in0({30{1'b0}}), .in1(30'h41), .in2(30'h47), .in3(30'h5f), .in4(30'h82087f), .in5(30'hc2087f),
    .in6(30'h8c2087f), .in7(30'h8c2887f), .in8(30'h8f2887f), .in9(30'haf2887f), .in10(30'haf2a87f),
    .out(out_2), .sel(Number_of_wrong_guess));  // open: in11, in12, in13, in14, in15
endmodule
