// Logisim project 171044041.circ as structural Verilog: 3 circuits, main circuit Main FSM
module InputSync (
  input  Input,
  output Output
);

  wire and_1_out, and_2_out, clock_1_out, not_1_out, not_2_out, not_3_out, not_4_out, not_5_out;
  wire [1:0] and_3_out, Input_Synchronizer_q;

  Clock clock_1 (.out(clock_1_out));
  not not_1 (not_1_out, Input_Synchronizer_q[1]);
  not not_2 (not_2_out, Input_Synchronizer_q[0]);
  not not_3 (not_3_out, Input_Synchronizer_q[1]);
  not not_4 (not_4_out, Input_Synchronizer_q[0]);
  not not_5 (not_5_out, Input_Synchronizer_q[1]);
  Register #(.width(2)) Input_Synchronizer (
    .D(and_3_out), .en(1'b1), .Q(Input_Synchronizer_q), .clk(clock_1_out));  // open: clr
  and and_1 (and_1_out, not_1_out, Input_Synchronizer_q[0], Input);
  and and_2 (and_2_out, Input_Synchronizer_q[1], not_2_out, Input);
  and and_3 (and_3_out[0], not_3_out, not_4_out, Input);
  and and_4 (Output, not_5_out, Input_Synchronizer_q[0]);
  or or_1 (and_3_out[1], and_1_out, and_2_out);
endmodule

// ScrBrd FSM
module ScrBrd (
  input  I,
  input  RESET,
  output [3:0] _4Bit_Output
);

  wire and_1_out, and_2_out, and_3_out, and_4_out, and_5_out, and_6_out, and_7_out, and_8_out, and_9_out,
       and_10_out, and_11_out, and_12_out, and_13_out, clock_1_out, inputsync_1_output, not_1_out, not_2_out,
       not_3_out, not_4_out, not_5_out, not_6_out, not_7_out, not_8_out, not_9_out;
  wire [3:0] ScoreBoard_FSM_q;

  Clock clock_1 (.out(clock_1_out));
  InputSync inputsync_1 (.Input(I), .Output(inputsync_1_output));
  Register #(.width(4)) ScoreBoard_FSM (
    .D(_4Bit_Output), .en(1'b1), .Q(ScoreBoard_FSM_q), .clk(clock_1_out), .clr(RESET));
  and and_1 (and_1_out, inputsync_1_output, ScoreBoard_FSM_q[2], ScoreBoard_FSM_q[1], ScoreBoard_FSM_q[0]);
  not not_1 (not_1_out, inputsync_1_output);
  not not_2 (not_2_out, ScoreBoard_FSM_q[1]);
  not not_3 (not_3_out, ScoreBoard_FSM_q[0]);
  not not_4 (not_4_out, ScoreBoard_FSM_q[2]);
  not not_5 (not_5_out, inputsync_1_output);
  not not_6 (not_6_out, ScoreBoard_FSM_q[0]);
  not not_7 (not_7_out, ScoreBoard_FSM_q[1]);
  not not_8 (not_8_out, inputsync_1_output);
  not not_9 (not_9_out, ScoreBoard_FSM_q[0]);
  or or_1 (_4Bit_Output[3], ScoreBoard_FSM_q[3], and_1_out);
  and and_2 (and_2_out, not_1_out, ScoreBoard_FSM_q[2]);
  and and_3 (and_3_out, ScoreBoard_FSM_q[2], not_2_out);
  and and_4 (and_4_out, ScoreBoard_FSM_q[2], not_3_out);
  and and_5 (and_5_out, ScoreBoard_FSM_q[3], ScoreBoard_FSM_q[2]);
  and and_6 (and_6_out, inputsync_1_output, not_4_out, ScoreBoard_FSM_q[1], ScoreBoard_FSM_q[0]);
  and and_7 (and_7_out, not_5_out, ScoreBoard_FSM_q[1]);
  and and_8 (and_8_out, ScoreBoard_FSM_q[1], not_6_out);
  and and_9 (and_9_out, ScoreBoard_FSM_q[3], ScoreBoard_FSM_q[2], ScoreBoard_FSM_q[1]);
  and and_10 (and_10_out, inputsync_1_output, not_7_out, ScoreBoard_FSM_q[0]);
  and and_11 (and_11_out, not_8_out, ScoreBoard_FSM_q[0]);
  and and_12 (and_12_out, inputsync_1_output, not_9_out);
  and and_13 (and_13_out, inputsync_1_output, ScoreBoard_FSM_q[3], ScoreBoard_FSM_q[2], ScoreBoard_FSM_q[1]);
  or or_2 (_4Bit_Output[2], and_2_out, and_3_out, and_4_out, and_5_out, and_6_out);
  or or_3 (_4Bit_Output[1], and_7_out, and_8_out, and_9_out, and_10_out);
  or or_4 (_4Bit_Output[0], and_11_out, and_12_out, and_13_out);
endmodule

module Main_FSM (
);

  wire and_1_out, and_2_out, and_3_out, and_4_out, and_5_out, and_6_out, and_7_out, and_8_out, and_9_out,
       and_10_out, and_11_out, and_12_out, and_13_out, and_14_out, and_15_out, and_16_out, and_17_out,
       and_18_out, and_19_out, and_20_out, and_21_out, and_22_out, and_23_out, and_24_out, clock_1_out,
       inputsync_1_output, inputsync_2_output, not_1_out, not_2_out, not_3_out, not_4_out, not_5_out,
       not_6_out, not_7_out, not_8_out, not_9_out, not_10_out, not_11_out, not_12_out, not_13_out,
       not_14_out, not_15_out, not_16_out, not_17_out, not_18_out, not_19_out, not_20_out, not_21_out,
       not_22_out, not_23_out, not_24_out, not_25_out, not_26_out, not_27_out, not_28_out, not_29_out,
       not_30_out, not_31_out, not_32_out, not_33_out, not_34_out, not_35_out, not_36_out, not_37_out,
       not_38_out, not_39_out, not_40_out, not_41_out, not_42_out, Player_1_out, Player_2_out, RESET_out,
       ScoreBoard_RESET_out;
  wire [2:0] Main_FSM_q, N0_out;
  wire [3:0] scrbrd_1__4bit_output, scrbrd_2__4bit_output;

  Button Player_1 (.out(Player_1_out));
  Button Player_2 (.out(Player_2_out));
  Button RESET (.out(RESET_out));
  Button ScoreBoard_RESET (.out(ScoreBoard_RESET_out));
  InputSync inputsync_1 (.Input(Player_1_out), .Output(inputsync_1_output));
  InputSync inputsync_2 (.Input(Player_2_out), .Output(inputsync_2_output));
  Register #(.width(3)) Main_FSM (.D(N0_out), .en(1'b1), .Q(Main_FSM_q), .clk(clock_1_out), .clr(RESET_out));
  Clock clock_1 (.out(clock_1_out));
  not not_1 (not_1_out, Main_FSM_q[0]);
  not not_2 (not_2_out, Main_FSM_q[1]);
  not not_3 (not_3_out, Main_FSM_q[1]);
  not not_4 (not_4_out, Main_FSM_q[0]);
  not not_5 (not_5_out, Main_FSM_q[2]);
  not not_6 (not_6_out, Main_FSM_q[1]);
  not not_7 (not_7_out, Main_FSM_q[0]);
  not not_8 (not_8_out, Main_FSM_q[2]);
  not not_9 (not_9_out, Main_FSM_q[1]);
  not not_10 (not_10_out, Main_FSM_q[2]);
  not not_11 (not_11_out, Main_FSM_q[0]);
  not not_12 (not_12_out, Main_FSM_q[2]);
  not not_13 (not_13_out, inputsync_1_output);
  not not_14 (not_14_out, Main_FSM_q[1]);
  not not_15 (not_15_out, Main_FSM_q[1]);
  not not_16 (not_16_out, Main_FSM_q[0]);
  not not_17 (not_17_out, inputsync_1_output);
  not not_18 (not_18_out, Main_FSM_q[1]);
  not not_19 (not_19_out, Main_FSM_q[0]);
  not not_20 (not_20_out, Main_FSM_q[1]);
  and and_1 (and_1_out, Main_FSM_q[2], Main_FSM_q[1], not_1_out);
  and and_2 (and_2_out, Main_FSM_q[2], not_2_out, Main_FSM_q[0]);
  and and_3 (and_3_out, Main_FSM_q[2], not_3_out, not_4_out);
  and and_4 (and_4_out, not_5_out, not_6_out, not_7_out);
  and and_5 (and_5_out, not_8_out, not_9_out, Main_FSM_q[0]);
  and and_6 (and_6_out, not_10_out, Main_FSM_q[1], not_11_out);
  and and_7 (and_7_out, not_12_out, Main_FSM_q[1], Main_FSM_q[0]);
  and and_8 (and_8_out, not_13_out, Main_FSM_q[2], not_14_out);
  and and_9 (and_9_out, Main_FSM_q[2], not_15_out, Main_FSM_q[0]);
  and and_10 (and_10_out, Main_FSM_q[2], Main_FSM_q[1], not_16_out);
  and and_11 (and_11_out, inputsync_2_output, not_17_out, not_18_out, not_19_out);
  and and_12 (and_12_out, inputsync_2_output, Main_FSM_q[2], not_20_out);
  LED led_1 (.in(and_7_out));
  Hex_Digit_Display hex_digit_display_1 (.value(scrbrd_1__4bit_output));  // open: dp
  ScrBrd scrbrd_1 (.I(and_7_out), .RESET(ScoreBoard_RESET_out), ._4Bit_Output(scrbrd_1__4bit_output));
  or N2 (N0_out[2], and_8_out, and_9_out, and_10_out, and_11_out, and_12_out);
  LED led_2 (.in(and_6_out));
  LED led_3 (.in(and_4_out));
  LED led_4 (.in(and_5_out));
  LED led_5 (.in(and_3_out));
  LED led_6 (.in(and_1_out));
  LED led_7 (.in(and_2_out));
  Hex_Digit_Display hex_digit_display_2 (.value(scrbrd_2__4bit_output));  // open: dp
  ScrBrd scrbrd_2 (.I(and_1_out), .RESET(ScoreBoard_RESET_out), ._4Bit_Output(scrbrd_2__4bit_output));
  not not_21 (not_21_out, inputsync_2_output);
  not not_22 (not_22_out, Main_FSM_q[2]);
  not not_23 (not_23_out, Main_FSM_q[2]);
  not not_24 (not_24_out, Main_FSM_q[0]);
  not not_25 (not_25_out, inputsync_2_output);
  not not_26 (not_26_out, Main_FSM_q[2]);
  not not_27 (not_27_out, Main_FSM_q[2]);
  not not_28 (not_28_out, inputsync_1_output);
  not not_29 (not_29_out, Main_FSM_q[1]);
  and and_13 (and_13_out, not_21_out, not_22_out, Main_FSM_q[1]);
  and and_14 (and_14_out, not_23_out, Main_FSM_q[1], Main_FSM_q[0]);
  and and_15 (and_15_out, Main_FSM_q[2], Main_FSM_q[1], not_24_out);
  and and_16 (and_16_out, not_25_out, inputsync_1_output, not_26_out, Main_FSM_q[0]);
  and and_17 (and_17_out, inputsync_1_output, not_27_out, Main_FSM_q[1]);
  and and_18 (and_18_out, inputsync_2_output, not_28_out, Main_FSM_q[2], not_29_out, Main_FSM_q[0]);
  or N1 (N0_out[1], and_13_out, and_14_out, and_15_out, and_16_out, and_17_out, and_18_out);
  not not_30 (not_30_out, inputsync_2_output);
  not not_31 (not_31_out, inputsync_1_output);
  not not_32 (not_32_out, Main_FSM_q[1]);
  not not_33 (not_33_out, Main_FSM_q[2]);
  not not_34 (not_34_out, inputsync_2_output);
  not not_35 (not_35_out, Main_FSM_q[2]);
  not not_36 (not_36_out, Main_FSM_q[0]);
  not not_37 (not_37_out, inputsync_1_output);
  not not_38 (not_38_out, Main_FSM_q[2]);
  not not_39 (not_39_out, inputsync_1_output);
  not not_40 (not_40_out, Main_FSM_q[1]);
  not not_41 (not_41_out, Main_FSM_q[0]);
  not not_42 (not_42_out, Main_FSM_q[1]);
  and and_19 (and_19_out, not_30_out, not_31_out, not_32_out, Main_FSM_q[0]);
  and and_20 (and_20_out, not_33_out, Main_FSM_q[1], Main_FSM_q[0]);
  and and_21 (and_21_out, not_34_out, inputsync_1_output, not_35_out, not_36_out);
  and and_22 (and_22_out, inputsync_2_output, not_37_out, not_38_out, Main_FSM_q[1]);
  and and_23 (and_23_out, inputsync_2_output, not_39_out, Main_FSM_q[2], not_40_out, not_41_out);
  and and_24 (and_24_out, inputsync_2_output, inputsync_1_output, not_42_out, Main_FSM_q[0]);
  or N0 (N0_out[0], and_19_out, and_20_out, and_21_out, and_22_out, and_23_out, and_24_out);

  // Notes on the sheet:
  //   Player 1
  //            SCORE
  //   Player 2
endmodule
