// Logisim project 171044041_P2.circ as structural Verilog: 3 circuits, main circuit main
module main (
  input  [15:0] Input_A,
  input  [15:0] Input_B,
  output [15:0] RESULT
);

  wire CLK_out, control_unit_1_la, control_unit_1_lb, control_unit_1_lm, control_unit_1_lr,
       control_unit_1_rm, control_unit_1_sa, datapath_1_gt, GO_out;

  Button GO (.out(GO_out));
  Clock CLK (.out(CLK_out));
  Control_Unit control_unit_1 (
    .GO(GO_out), .GT(datapath_1_gt), .CLK(CLK_out), .Rm(control_unit_1_rm), .Lb(control_unit_1_lb),
    .La(control_unit_1_la), .Lm(control_unit_1_lm), .Sa(control_unit_1_sa), .Lr(control_unit_1_lr));  // open: out_10
  DataPath datapath_1 (
    .A_IN(Input_A), .B_IN(Input_B), .Lm(control_unit_1_lm), .Rm(control_unit_1_rm), .Sa(control_unit_1_sa),
    .La(control_unit_1_la), .Lb(control_unit_1_lb), .Lr(control_unit_1_lr), .CLK(CLK_out), .Result(RESULT),
    .gt(datapath_1_gt));  // open: ngt
  Hex_Digit_Display hex_digit_display_1 (.value(RESULT[15:12]));  // open: dp
  Hex_Digit_Display hex_digit_display_2 (.value(RESULT[11:8]));  // open: dp
  Hex_Digit_Display hex_digit_display_3 (.value(RESULT[7:4]));  // open: dp
  Hex_Digit_Display hex_digit_display_4 (.value(RESULT[3:0]));  // open: dp

  // Notes on the sheet:
  //   HEXADECIMAL RESULT
endmodule

module DataPath (
  input  [15:0] A_IN,
  input  [15:0] B_IN,
  input  Lm,
  input  Rm,
  input  Sa,
  input  La,
  input  Lb,
  input  Lr,
  input  CLK,
  output [15:0] Result,
  output gt,
  output ngt
);

  wire comparator_1_eq, comparator_1_lt;
  wire [15:0] A_q, adder_1_out, MULT_q, multiplexer_1_out, multiplexer_2_out, multiplexer_3_out, register_1_q;

  Register #(.width(16)) MULT (.D(adder_1_out), .en(Lm), .Q(MULT_q), .clk(CLK), .clr(Rm));
  Multiplexer #(.width(16), .enable("false")) multiplexer_1 (
    .in0(MULT_q), .in1(A_q), .out(multiplexer_1_out), .sel(Sa));
  Multiplexer #(.width(16), .enable("false")) multiplexer_2 (
    .in0(register_1_q), .in1({16{1'b1}}), .out(multiplexer_2_out), .sel(Sa));
  Adder #(.width(16)) adder_1 (.a(multiplexer_1_out), .b(multiplexer_2_out), .out(adder_1_out));  // open: cin, cout
  Multiplexer #(.width(16), .enable("false")) multiplexer_3 (
    .in0(A_IN), .in1(adder_1_out), .out(multiplexer_3_out), .sel(Sa));
  Register #(.width(16)) A (.D(multiplexer_3_out), .en(La), .Q(A_q), .clk(CLK));  // open: clr
  Comparator #(.width(16)) comparator_1 (.a(A_q), .b({16{1'b0}}), .gt(gt), .eq(comparator_1_eq), .lt(comparator_1_lt));
  or or_1 (ngt, comparator_1_eq, comparator_1_lt);
  Register #(.width(16)) register_1 (.D(B_IN), .en(Lb), .Q(register_1_q), .clk(CLK));  // open: clr
  Register #(.width(16)) register_2 (.D(MULT_q), .en(Lr), .Q(Result), .clk(CLK));  // open: clr
endmodule

module Control_Unit (
  input  GO,
  input  GT,
  input  CLK,
  output Rm,
  output Lb,
  output La,
  output Lm,
  output Sa,
  output Lr,
  output [2:0] out_10
);

  wire and_1_out, and_2_out, and_3_out, and_4_out, and_5_out, and_6_out, and_7_out, and_9_out, and_10_out,
       not_1_out, not_2_out, not_3_out, not_4_out, not_5_out, not_6_out, not_7_out, not_8_out, not_9_out,
       not_10_out, not_11_out, not_12_out, not_13_out, not_14_out, not_15_out, not_16_out, not_17_out,
       not_18_out, not_19_out, not_20_out, not_21_out, not_22_out, not_23_out;
  wire [2:0] or_3_out;

  not not_1 (not_1_out, out_10[2]);
  not not_2 (not_2_out, GT);
  not not_3 (not_3_out, out_10[2]);
  not not_4 (not_4_out, out_10[2]);
  not not_5 (not_5_out, out_10[0]);
  and and_1 (and_1_out, not_1_out, out_10[1], not_2_out);
  and and_2 (and_2_out, not_3_out, out_10[1], out_10[0]);
  not not_6 (not_6_out, out_10[2]);
  not not_7 (not_7_out, out_10[1]);
  and and_3 (and_3_out, not_6_out, not_7_out, out_10[0]);
  and and_4 (and_4_out, not_4_out, out_10[1], not_5_out, GT);
  not not_8 (not_8_out, out_10[1]);
  and and_5 (and_5_out, out_10[2], not_8_out, not_9_out);
  not not_9 (not_9_out, out_10[0]);
  not not_10 (not_10_out, out_10[2]);
  not not_11 (not_11_out, out_10[0]);
  and and_6 (and_6_out, not_10_out, not_11_out, GO);
  not not_12 (not_12_out, out_10[2]);
  and and_7 (and_7_out, not_12_out, out_10[1], not_13_out);
  not not_13 (not_13_out, out_10[0]);
  or or_1 (or_3_out[2], and_1_out, and_2_out);
  or or_2 (or_3_out[1], and_3_out, and_4_out, and_5_out);
  or or_3 (or_3_out[0], and_6_out, and_7_out);
  Register #(.width(3)) register_1 (.D(or_3_out), .en(1'b1), .Q(out_10), .clk(CLK));  // open: clr
  not not_14 (not_14_out, out_10[2]);
  not not_15 (not_15_out, out_10[1]);
  not not_16 (not_16_out, out_10[2]);
  not not_17 (not_17_out, out_10[1]);
  not not_18 (not_18_out, out_10[1]);
  not not_19 (not_19_out, out_10[0]);
  not not_20 (not_20_out, out_10[2]);
  not not_21 (not_21_out, out_10[1]);
  not not_22 (not_22_out, out_10[0]);
  not not_23 (not_23_out, out_10[1]);
  and and_8 (Lb, not_14_out, not_15_out, out_10[0]);
  and and_9 (and_9_out, not_16_out, not_17_out, out_10[0]);
  or or_4 (La, and_9_out, and_10_out);
  and and_10 (and_10_out, out_10[2], not_18_out, not_19_out);
  and and_11 (Lm, not_20_out, out_10[1], out_10[0]);
  and and_12 (Sa, out_10[2], not_21_out, not_22_out);
  and and_13 (Lr, out_10[2], not_23_out, out_10[0]);

  assign Rm = Lb;
endmodule
